# Fritzing sketch prototipo (saved by Fritzing 0.9.3b)
perfboards: 1

parts:
  Componente1 = Arduino Uno (Rev3)
  T1 = LM35 Temperature Sensor [package="TO92 [THT]"]
  T2 = LM35 Temperature Sensor [package="TO92 [THT]"]
  R1 = Resistor [tolerance=±5% resistance=4.7k package=THT]
  R2 = Resistor [tolerance=±5% resistance=4.7k package=THT]
  LCD1 = LCD screen  # not connected
  IC1 = IC, DIP package, 8 pins [chip_label=I2C]

nets:
  N1: Componente1.A4/SDA, IC1.pin6
  N2: Componente1.A5/SCL, IC1.pin5
  N3: Componente1.D2, T1.Vout, R1.Pin_0
  N4: Componente1.D4, T2.Vout, R2.Pin_1
  N5: Componente1.5V, T2.+Vs

notes:
  T1
  T2
